# Fritzing sketch ArduinoPIUAux_Lights (saved by Fritzing 0.9.3b)
breadboards: 1

parts:
  Part1 = Arduino Uno (Rev3)
  S1 = Pushbutton [package=THT]
  S2 = Pushbutton [package=THT]
  S3 = Pushbutton [package=THT]
  S4 = Pushbutton [package=THT]
  LED1 = LED - 5mm [color="Red (633nm)" package="5 mm [THT]"]
  Q1 = Basic FET N-Channel [package="TO220 [THT]"]
  U1 = 74HC595 [package="DIP16 [THT]"]
  U2 = 74HC595 [package="DIP16 [THT]"]
  U3 = 74HC595 [package="DIP16 [THT]"]
  R1 = Resistor [tolerance=±5% resistance=10k package=THT]
  R2 = Resistor [tolerance=±5% resistance=10k package=THT]
  S6 = Round Pushbutton

nets:
  N1: Part1.A0, S6.leg1
  N2: Part1.A3, U1.DS
  N3: Part1.A4/SDA, U1.ST_CP, U2.ST_CP, U3.ST_CP
  N4: Part1.A5/SCL, U1.SH_CP, U2.SH_CP, U3.SH_CP
  N5: Part1.D2, S1.leg0, S2.leg0, S3.leg0, S4.leg0, R1.Pin_1
  VCC: Part1.5V, S1.leg1, S2.leg1, S3.leg1, S4.leg1, U1.MR, U1.VCC, U2.MR, U2.VCC, U3.VCC
  GND: Part1.GND, Q1.source, U1.GND, U1.OE, U2.GND, U2.OE, U3.GND, U3.OE, R1.Pin_0, R2.Pin_0, S6.leg0
  N6: LED1.cathode, Q1.drain
  N7: Q1.gate, U1.Q0, R2.Pin_1
  N8: U1.Q7', U2.DS
  N9: U2.Q7', U3.DS

notes:
  Pad sensors: All four sensors in each
  Panel lights: Light hooked up to +12V, ground controlled by MOSFET
  Additional panel sensors/lights not shown, hook them up like you did with the first ones
  To panel lights
  (Each shift register = 1 player)
  To cabinet lights (See wiring.md for more info)
  Cabinet switches (test, service, etc):
  To cabinet +12V and ground
  (See wiring.md)
  To panel sensor groups
  panel wired in parallel
